# Fritzing sketch Pressure Cuff (saved by Fritzing 0.9.3b)
circuit board: 8.5cm x 4.27822cm
breadboards: 1

parts:
  R2 = Resistor [tolerance=±5% resistance=10k package=THT]  # not connected
  R3 = Resistor [tolerance=±5% resistance=47 package=THT]  # not connected
  R4 = Resistor [tolerance=±5% resistance=1.5 package=THT]  # not connected
  R5 = Resistor [tolerance=±5% resistance=1.5 package=THT]  # not connected
  R6 = Resistor [tolerance=±5% resistance=47 package=THT]  # not connected
  R7 = Resistor [tolerance=±5% resistance=15 package=THT]  # not connected
  U1 = LM 358 Dual Op-Amp [package="DIP8 [THT]"]
  J2 = female pin header, 2 pins [form="♀ (female)"]
  J3 = female pin header, 2 pins [form="♀ (female)"]
  Part1 = Adafruit PiTFT Plus 2.8inch [part_number="Adafruit #2298 and #2423"]  # not connected
  J4 = Generic double row SMD male header - 8 pins [form="♂ (male)" package=THT]

nets:
  N1: U1.connector3, J2.pin1, J4.pin3
  N2: U1.connector7, J3.pin2, J4.pin2
  N3: J2.pin2, J3.pin1

notes:
  +
  -
  Vs
  GND
  Vout
  Aout
  Ain (Invt)
  Ain (!Invt)
  V+
  Bout
  Bin (Invt)
  Bin (!Invt)

custom parts:
  Adafruit PiTFT Plus 2.8inch: Is this not the cutest little display for the Raspberry Pi? It features a 2.8" display with 320x240 16-bit color pixels and a resistive touch overlay. The plate uses the high speed SPI interface on the Pi and can use the mini display as a console, X window port, displaying images or video etc. Best of all it plugs right in on top! This updated design fits perfectly onto the Pi Zero, Pi 3, Pi 2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
  Generic double row SMD male header - 8 pins: Generic double row SMD male header
